# Fritzing sketch cylon (saved by Fritzing 0.9.3b)
breadboards: 1

parts:
  R1 = Resistor [tolerance=±5% resistance=220 package=THT]
  R2 = Resistor [tolerance=±5% resistance=220 package=THT]
  R3 = Resistor [tolerance=±5% resistance=220 package=THT]
  R4 = Resistor [tolerance=±5% resistance=220 package=THT]
  R5 = Resistor [tolerance=±5% resistance=220 package=THT]
  R6 = Resistor [tolerance=±5% resistance=220 package=THT]
  R7 = Resistor [tolerance=±5% resistance=220 package=THT]
  R8 = Resistor [tolerance=±5% resistance=220 package=THT]
  Part1 = Arduino Uno (Rev3)
  LED1 = LED - 5mm [color="Red (633nm)" package="5 mm [THT]"]
  LED2 = LED - 5mm [color="Red (633nm)" package="5 mm [THT]"]
  LED3 = LED - 5mm [color="Red (633nm)" package="5 mm [THT]"]
  LED4 = LED - 5mm [color="Red (633nm)" package="5 mm [THT]"]
  LED5 = LED - 5mm [color="Red (633nm)" package="5 mm [THT]"]
  LED6 = LED - 5mm [color="Red (633nm)" package="5 mm [THT]"]
  LED7 = LED - 5mm [color="Red (633nm)" package="5 mm [THT]"]
  LED8 = LED - 5mm [color="Red (633nm)" package="5 mm [THT]"]

nets:
  N1: R1.Pin_0, Part1.D10_PWM/SS
  N2: R1.Pin_1, LED3.anode
  N3: R2.Pin_0, Part1.D9_PWM
  N4: R2.Pin_1, LED2.anode
  N5: R3.Pin_0, Part1.D11_PWM/MOSI
  N6: R3.Pin_1, LED4.anode
  N7: R4.Pin_0, Part1.D12/MISO
  N8: R4.Pin_1, LED1.anode
  N9: R5.Pin_0, Part1.D8
  N10: R5.Pin_1, LED6.anode
  N11: R6.Pin_0, Part1.D7
  N12: R6.Pin_1, LED8.anode
  N13: R7.Pin_0, Part1.D6_PWM
  N14: R7.Pin_1, LED5.anode
  N15: R8.Pin_0, Part1.D5_PWM
  N16: R8.Pin_1, LED7.anode
  N17: Part1.GND, LED1.cathode, LED2.cathode, LED3.cathode, LED4.cathode, LED5.cathode, LED6.cathode, LED7.cathode, LED8.cathode
